// Digital circuit 10-bit PISO.dig as structural Verilog
module _10_bit_PISO (
  input  CLK,
  input  Load,
  input  S9,
  input  S8,
  input  S7,
  input  S6,
  input  S5,
  input  S4,
  input  S3,
  input  S2,
  input  S1,
  input  S0,
  output o_p
);

  wire d_ff_as_1_q, d_ff_as_2_q, d_ff_as_3_q, d_ff_as_4_q, d_ff_as_5_q, d_ff_as_6_q, d_ff_as_7_q,
       d_ff_as_8_q, d_ff_as_9_q, multiplexer_1_out, multiplexer_2_out, multiplexer_3_out, multiplexer_4_out,
       multiplexer_5_out, multiplexer_6_out, multiplexer_7_out, multiplexer_8_out, multiplexer_9_out,
       multiplexer_10_out;

  Multiplexer multiplexer_1 (.sel(Load), .in_0(1'b0), .in_1(S9), .out(multiplexer_1_out));
  D_FF_AS d_ff_as_1 (.Set(1'b0), .D(multiplexer_1_out), .C(CLK), .Clr(1'b0), .Q(d_ff_as_1_q));  // open: nQ
  Multiplexer multiplexer_2 (.sel(Load), .in_0(d_ff_as_1_q), .in_1(S8), .out(multiplexer_2_out));
  D_FF_AS d_ff_as_2 (.Set(1'b0), .D(multiplexer_2_out), .C(CLK), .Clr(1'b0), .Q(d_ff_as_2_q));  // open: nQ
  Multiplexer multiplexer_3 (.sel(Load), .in_0(d_ff_as_2_q), .in_1(S7), .out(multiplexer_3_out));
  D_FF_AS d_ff_as_3 (.Set(1'b0), .D(multiplexer_3_out), .C(CLK), .Clr(1'b0), .Q(d_ff_as_3_q));  // open: nQ
  Multiplexer multiplexer_4 (.sel(Load), .in_0(d_ff_as_3_q), .in_1(S6), .out(multiplexer_4_out));
  D_FF_AS d_ff_as_4 (.Set(1'b0), .D(multiplexer_4_out), .C(CLK), .Clr(1'b0), .Q(d_ff_as_4_q));  // open: nQ
  Multiplexer multiplexer_5 (.sel(Load), .in_0(d_ff_as_4_q), .in_1(S5), .out(multiplexer_5_out));
  D_FF_AS d_ff_as_5 (.Set(1'b0), .D(multiplexer_5_out), .C(CLK), .Clr(1'b0), .Q(d_ff_as_5_q));  // open: nQ
  Multiplexer multiplexer_6 (.sel(Load), .in_0(d_ff_as_5_q), .in_1(S4), .out(multiplexer_6_out));
  D_FF_AS d_ff_as_6 (.Set(1'b0), .D(multiplexer_6_out), .C(CLK), .Clr(1'b0), .Q(d_ff_as_6_q));  // open: nQ
  Multiplexer multiplexer_7 (.sel(Load), .in_0(d_ff_as_6_q), .in_1(S3), .out(multiplexer_7_out));
  D_FF_AS d_ff_as_7 (.Set(1'b0), .D(multiplexer_7_out), .C(CLK), .Clr(1'b0), .Q(d_ff_as_7_q));  // open: nQ
  Multiplexer multiplexer_8 (.sel(Load), .in_0(d_ff_as_7_q), .in_1(S2), .out(multiplexer_8_out));
  D_FF_AS d_ff_as_8 (.Set(1'b0), .D(multiplexer_8_out), .C(CLK), .Clr(1'b0), .Q(d_ff_as_8_q));  // open: nQ
  Multiplexer multiplexer_9 (.sel(Load), .in_0(d_ff_as_8_q), .in_1(S1), .out(multiplexer_9_out));
  D_FF_AS d_ff_as_9 (.Set(1'b0), .D(multiplexer_9_out), .C(CLK), .Clr(1'b0), .Q(d_ff_as_9_q));  // open: nQ
  Multiplexer multiplexer_10 (.sel(Load), .in_0(d_ff_as_9_q), .in_1(S0), .out(multiplexer_10_out));
  D_FF_AS d_ff_as_10 (.Set(1'b0), .D(multiplexer_10_out), .C(CLK), .Clr(1'b0), .Q(o_p));  // open: nQ
endmodule
