// Digital circuit Embedded Mod 100 Counter.dig as structural Verilog
module Embedded_Mod_100_Counter (
  input  CLK,
  input  CLR,
  output Q,
  output A0,
  output A1,
  output A2,
  output A3,
  output B0,
  output B1,
  output B2,
  output B3
);

  wire and_1_out, and_2_out, jk_ff_as_1_nq, jk_ff_as_2_nq, jk_ff_as_3_nq, jk_ff_as_4_nq, jk_ff_as_5_nq,
       jk_ff_as_6_nq, jk_ff_as_7_nq, not_1_out, not_2_out, not_3_out, not_4_out, or_1_out, or_2_out;

  JK_FF_AS jk_ff_as_1 (.Set(1'b0), .J(1'b1), .C(CLK), .K(1'b1), .Clr(or_1_out), .Q(A0), .nQ(jk_ff_as_1_nq));
  JK_FF_AS jk_ff_as_2 (.Set(1'b0), .J(1'b1), .C(jk_ff_as_1_nq), .K(1'b1), .Clr(or_1_out), .Q(A1), .nQ(jk_ff_as_2_nq));
  JK_FF_AS jk_ff_as_3 (.Set(1'b0), .J(1'b1), .C(jk_ff_as_2_nq), .K(1'b1), .Clr(or_1_out), .Q(A2), .nQ(jk_ff_as_3_nq));
  JK_FF_AS jk_ff_as_4 (.Set(1'b0), .J(1'b1), .C(jk_ff_as_3_nq), .K(1'b1), .Clr(or_1_out), .Q(A3), .nQ(jk_ff_as_4_nq));
  or or_1 (or_1_out, or_2_out, and_1_out);
  not not_1 (not_1_out, A0);
  and and_1 (and_1_out, A3, not_2_out, A1, not_1_out);
  not not_2 (not_2_out, A2);
  JK_FF_AS jk_ff_as_5 (.Set(1'b0), .J(1'b1), .C(jk_ff_as_4_nq), .K(1'b1), .Clr(or_2_out), .Q(B0), .nQ(jk_ff_as_5_nq));
  JK_FF_AS jk_ff_as_6 (.Set(1'b0), .J(1'b1), .C(jk_ff_as_5_nq), .K(1'b1), .Clr(or_2_out), .Q(B1), .nQ(jk_ff_as_6_nq));
  JK_FF_AS jk_ff_as_7 (.Set(1'b0), .J(1'b1), .C(jk_ff_as_6_nq), .K(1'b1), .Clr(or_2_out), .Q(B2), .nQ(jk_ff_as_7_nq));
  JK_FF_AS jk_ff_as_8 (.Set(1'b0), .J(1'b1), .C(jk_ff_as_7_nq), .K(1'b1), .Clr(or_2_out), .Q(B3), .nQ(Q));
  or or_2 (or_2_out, CLR, and_2_out);
  not not_3 (not_3_out, B0);
  and and_2 (and_2_out, B3, not_4_out, B1, not_3_out);
  not not_4 (not_4_out, B2);
endmodule
