// Digital circuit MOD 60 Counter.dig as structural Verilog
module MOD_60_Counter (
  input  clk
);

  wire _7448_1_pin9, _7448_1_pin10, _7448_1_pin11, _7448_1_pin12, _7448_1_pin13, _7448_1_pin14,
       _7448_1_pin15, _7448_2_pin9, _7448_2_pin10, _7448_2_pin11, _7448_2_pin12, _7448_2_pin13,
       _7448_2_pin14, _7448_2_pin15, _7490_1_pin1, _7490_1_pin2, _7490_1_pin3, _7490_1_pin11, _7490_1_pin14,
       _7490_2_pin1, _7490_2_pin3, _7490_2_pin8;

  _7490 _7490_1 (
    .pin1(_7490_1_pin1), .pin2(_7490_1_pin2), .pin3(_7490_1_pin3), .pin5(1'b1), .pin6(1'b0), .pin7(1'b0),
    .pin8(_7490_1_pin3), .pin9(_7490_1_pin2), .pin10(1'b0), .pin11(_7490_1_pin11), .pin12(_7490_1_pin1),
    .pin14(_7490_1_pin14));  // open: pin4, pin13
  _7490 _7490_2 (
    .pin1(_7490_2_pin1), .pin2(_7490_1_pin14), .pin3(_7490_2_pin3), .pin5(1'b1), .pin6(1'b0), .pin7(1'b0),
    .pin8(_7490_2_pin8), .pin9(_7490_2_pin3), .pin10(1'b0), .pin11(_7490_1_pin14), .pin12(_7490_2_pin1),
    .pin14(clk));  // open: pin4, pin13
  _7448 _7448_1 (
    .pin1(_7490_1_pin2), .pin2(_7490_1_pin3), .pin3(1'b1), .pin4(1'b1), .pin5(1'b1), .pin6(_7490_1_pin11),
    .pin7(_7490_1_pin1), .pin8(1'b0), .pin9(_7448_1_pin9), .pin10(_7448_1_pin10), .pin11(_7448_1_pin11),
    .pin12(_7448_1_pin12), .pin13(_7448_1_pin13), .pin14(_7448_1_pin14), .pin15(_7448_1_pin15), .pin16(1'b1));
  _7448 _7448_2 (
    .pin1(_7490_2_pin3), .pin2(_7490_2_pin8), .pin3(1'b1), .pin4(1'b1), .pin5(1'b1), .pin6(_7490_1_pin14),
    .pin7(_7490_2_pin1), .pin8(1'b0), .pin9(_7448_2_pin9), .pin10(_7448_2_pin10), .pin11(_7448_2_pin11),
    .pin12(_7448_2_pin12), .pin13(_7448_2_pin13), .pin14(_7448_2_pin14), .pin15(_7448_2_pin15), .pin16(1'b1));
  Seven_Seg seven_seg_1 (
    .a(_7448_1_pin13), .b(_7448_1_pin12), .c(_7448_1_pin11), .d(_7448_1_pin10), .e(_7448_1_pin9),
    .f(_7448_1_pin15), .g(_7448_1_pin14), .dp(1'b0));
  Seven_Seg seven_seg_2 (
    .a(_7448_2_pin13), .b(_7448_2_pin12), .c(_7448_2_pin11), .d(_7448_2_pin10), .e(_7448_2_pin9),
    .f(_7448_2_pin15), .g(_7448_2_pin14), .dp(1'b0));

  // Notes on the sheet:
  //   clk: Hz: 3
endmodule
