// Digital circuit Mod 16.dig as structural Verilog
module Mod_16 (
  input  CLK,
  input  CLR,
  input  Up,
  output A0,
  output A3,
  output A2,
  output A1
);

  wire jk_ff_as_1_nq, jk_ff_as_2_nq, jk_ff_as_3_nq, multiplexer_1_out, multiplexer_2_out, multiplexer_3_out;

  JK_FF_AS jk_ff_as_1 (.Set(1'b0), .J(1'b1), .C(CLK), .K(1'b1), .Clr(CLR), .Q(A0), .nQ(jk_ff_as_1_nq));
  Multiplexer multiplexer_1 (.sel(Up), .in_0(A0), .in_1(jk_ff_as_1_nq), .out(multiplexer_1_out));
  JK_FF_AS jk_ff_as_2 (.Set(1'b0), .J(1'b1), .C(multiplexer_1_out), .K(1'b1), .Clr(CLR), .Q(A1), .nQ(jk_ff_as_2_nq));
  Multiplexer multiplexer_2 (.sel(Up), .in_0(A1), .in_1(jk_ff_as_2_nq), .out(multiplexer_2_out));
  JK_FF_AS jk_ff_as_3 (.Set(1'b0), .J(1'b1), .C(multiplexer_2_out), .K(1'b1), .Clr(CLR), .Q(A2), .nQ(jk_ff_as_3_nq));
  Multiplexer multiplexer_3 (.sel(Up), .in_0(A2), .in_1(jk_ff_as_3_nq), .out(multiplexer_3_out));
  JK_FF_AS jk_ff_as_4 (.Set(1'b0), .J(1'b1), .C(multiplexer_3_out), .K(1'b1), .Clr(CLR), .Q(A3));  // open: nQ
endmodule
