// Digital circuit Non Overlapping 101 sequence detector.dig as structural Verilog
module Non_Overlapping_101_sequence_detector (
  input  Load,
  input  in_2,
  input  in_3,
  input  in_4,
  input  in_5,
  input  in_6,
  input  clk,
  input  in_8,
  input  in_9,
  input  in_10,
  input  in_11,
  input  in_12
);

  wire _7448_1_pin1, _7448_1_pin2, _7448_1_pin6, _7448_1_pin7, _7448_1_pin9, _7448_1_pin10, _7448_1_pin11,
       _7448_1_pin12, _7448_1_pin13, _7448_1_pin14, _7448_1_pin15, and_1_out, and_2_out, and_3_out, FF0_q,
       FF1_nq, FF1_q, not_1_out, undriven;

  _10_bit_PISO _10_bit_piso_1 ();
  not not_1 (not_1_out, undriven);
  and and_1 (and_1_out, FF0_q, not_1_out);
  D_FF_AS FF1 (.Set(1'b0), .D(and_1_out), .C(clk), .Clr(Load), .Q(FF1_q), .nQ(FF1_nq));
  and and_2 (and_2_out, FF1_nq, undriven);
  and and_3 (and_3_out, undriven, FF1_q);
  D_FF_AS FF0 (.Set(1'b0), .D(and_2_out), .C(clk), .Clr(Load), .Q(FF0_q));  // open: nQ
  Mod_16 mod_16_1 ();
  _7448 _7448_1 (
    .pin1(_7448_1_pin1), .pin2(_7448_1_pin2), .pin3(1'b1), .pin4(1'b1), .pin5(1'b1), .pin6(_7448_1_pin6),
    .pin7(_7448_1_pin7), .pin8(1'b0), .pin9(_7448_1_pin9), .pin10(_7448_1_pin10), .pin11(_7448_1_pin11),
    .pin12(_7448_1_pin12), .pin13(_7448_1_pin13), .pin14(_7448_1_pin14), .pin15(_7448_1_pin15), .pin16(1'b1));
  Seven_Seg seven_seg_1 (
    .a(_7448_1_pin13), .b(_7448_1_pin12), .c(_7448_1_pin11), .d(_7448_1_pin10), .e(_7448_1_pin9),
    .f(_7448_1_pin15), .g(_7448_1_pin14), .dp(1'b0));

  // Notes on the sheet:
  //   clk: Hz: 5
endmodule
