// Digital circuit Serial Adder Circuit.dig as structural Verilog
module Serial_Adder_Circuit (
  input  A,
  input  B,
  input  CLK,
  input  CLR
);

  wire _7483_1_p1, _7483_1_p4, _7483_1_p5;

  // _7483 _7483_1: pin names not known; wires that end beside it: _7483_1_p1, B, A, _7483_1_p4, _7483_1_p5
  LED led_1 (.in(_7483_1_p1));
  D_FF_AS d_ff_as_1 (.Set(1'b0), .D(_7483_1_p1), .C(CLK), .Clr(CLR), .Q(_7483_1_p5));  // open: nQ
  LED led_2 (.in(_7483_1_p4));
  LED led_3 (.in(_7483_1_p5));
endmodule
