// Digital circuit Stopwatch with ms.dig as structural Verilog
module Stopwatch_with_ms (
  input  CLK,
  input  START,
  input  CLR
);

  wire _7448_1_pin1, _7448_1_pin2, _7448_1_pin6, _7448_1_pin7, _7448_1_pin9, _7448_1_pin10, _7448_1_pin11,
       _7448_1_pin12, _7448_1_pin13, _7448_1_pin14, _7448_1_pin15, _7448_2_pin1, _7448_2_pin7, _7448_2_pin9,
       _7448_2_pin10, _7448_2_pin11, _7448_2_pin12, _7448_2_pin13, _7448_2_pin14, _7448_2_pin15,
       _7448_3_pin9, _7448_3_pin10, _7448_3_pin11, _7448_3_pin12, _7448_3_pin13, _7448_3_pin14,
       _7448_3_pin15, _7448_4_pin1, _7448_4_pin2, _7448_4_pin9, _7448_4_pin10, _7448_4_pin11, _7448_4_pin12,
       _7448_4_pin13, _7448_4_pin14, _7448_4_pin15, _7448_5_pin1, _7448_5_pin2, _7448_5_pin6, _7448_5_pin7,
       _7448_5_pin9, _7448_5_pin10, _7448_5_pin11, _7448_5_pin12, _7448_5_pin13, _7448_5_pin14,
       _7448_5_pin15, _7448_6_pin1, _7448_6_pin2, _7448_6_pin9, _7448_6_pin10, _7448_6_pin11, _7448_6_pin12,
       _7448_6_pin13, _7448_6_pin14, _7448_6_pin15, _7448_7_pin1, _7448_7_pin2, _7448_7_pin6, _7448_7_pin7,
       _7448_7_pin9, _7448_7_pin10, _7448_7_pin11, _7448_7_pin12, _7448_7_pin13, _7448_7_pin14,
       _7448_7_pin15, _7448_8_pin6, _7448_8_pin9, _7448_8_pin10, _7448_8_pin11, _7448_8_pin12, _7448_8_pin13,
       _7448_8_pin14, _7448_8_pin15, embedded_mod_24_counter_1_p1, embedded_mod_60_counter_1_p2,
       embedded_mod_60_counter_1_p4, embedded_mod_60_counter_1_p5, embedded_mod_60_counter_1_p6,
       embedded_mod_60_counter_1_p7, embedded_mod_60_counter_1_p8, embedded_mod_60_counter_1_p9,
       embedded_mod_60_counter_2_p2, embedded_mod_60_counter_2_p5, embedded_mod_60_counter_2_p10,
       embedded_mod_100_counter_1_p5, embedded_mod_100_counter_1_p10, embedded_mod_100_counter_1_p11,
       embedded_mod_100_counter_1_p12;

  _7448 _7448_1 (
    .pin1(_7448_1_pin1), .pin2(_7448_1_pin2), .pin3(1'b1), .pin4(1'b1), .pin5(1'b1), .pin6(_7448_1_pin6),
    .pin7(_7448_1_pin7), .pin8(1'b0), .pin9(_7448_1_pin9), .pin10(_7448_1_pin10), .pin11(_7448_1_pin11),
    .pin12(_7448_1_pin12), .pin13(_7448_1_pin13), .pin14(_7448_1_pin14), .pin15(_7448_1_pin15), .pin16(1'b1));
  // Embedded_Mod_24_Counter embedded_mod_24_counter_1: pin names not known; wires that end beside it: embedded_mod_24_counter_1_p1, _7448_1_pin7, _7448_1_pin1, _7448_1_pin2, _7448_1_pin6
  Seven_Seg seven_seg_1 (
    .a(_7448_2_pin13), .b(_7448_2_pin12), .c(_7448_2_pin11), .d(_7448_2_pin10), .e(_7448_2_pin9),
    .f(_7448_2_pin15), .g(_7448_2_pin14), .dp(1'b0));
  Seven_Seg seven_seg_2 (
    .a(_7448_1_pin13), .b(_7448_1_pin12), .c(_7448_1_pin11), .d(_7448_1_pin10), .e(_7448_1_pin9),
    .f(_7448_1_pin15), .g(_7448_1_pin14), .dp(1'b0));
  _7448 _7448_2 (
    .pin1(_7448_2_pin1), .pin2(1'b0), .pin3(1'b1), .pin4(1'b1), .pin5(1'b1), .pin6(1'b0),
    .pin7(_7448_2_pin7), .pin8(1'b0), .pin9(_7448_2_pin9), .pin10(_7448_2_pin10), .pin11(_7448_2_pin11),
    .pin12(_7448_2_pin12), .pin13(_7448_2_pin13), .pin14(_7448_2_pin14), .pin15(_7448_2_pin15), .pin16(1'b1));
  // Embedded_Mod_60_Counter embedded_mod_60_counter_1: pin names not known; wires that end beside it: _7448_2_pin7, embedded_mod_60_counter_1_p2, _7448_2_pin1, embedded_mod_60_counter_1_p4, embedded_mod_60_counter_1_p5, embedded_mod_60_counter_1_p6, embedded_mod_60_counter_1_p7, embedded_mod_60_counter_1_p8, embedded_mod_60_counter_1_p9
  _7448 _7448_3 (
    .pin1(embedded_mod_60_counter_1_p6), .pin2(embedded_mod_60_counter_1_p7), .pin3(1'b1), .pin4(1'b1),
    .pin5(1'b1), .pin6(embedded_mod_60_counter_1_p8), .pin7(embedded_mod_60_counter_1_p5), .pin8(1'b0),
    .pin9(_7448_3_pin9), .pin10(_7448_3_pin10), .pin11(_7448_3_pin11), .pin12(_7448_3_pin12),
    .pin13(_7448_3_pin13), .pin14(_7448_3_pin14), .pin15(_7448_3_pin15), .pin16(1'b1));
  Seven_Seg seven_seg_3 (
    .a(_7448_4_pin13), .b(_7448_4_pin12), .c(_7448_4_pin11), .d(_7448_4_pin10), .e(_7448_4_pin9),
    .f(_7448_4_pin15), .g(_7448_4_pin14), .dp(1'b0));
  Seven_Seg seven_seg_4 (
    .a(_7448_3_pin13), .b(_7448_3_pin12), .c(_7448_3_pin11), .d(_7448_3_pin10), .e(_7448_3_pin9),
    .f(_7448_3_pin15), .g(_7448_3_pin14), .dp(1'b0));
  _7448 _7448_4 (
    .pin1(_7448_4_pin1), .pin2(_7448_4_pin2), .pin3(1'b1), .pin4(1'b1), .pin5(1'b1), .pin6(1'b0),
    .pin7(embedded_mod_60_counter_1_p9), .pin8(1'b0), .pin9(_7448_4_pin9), .pin10(_7448_4_pin10),
    .pin11(_7448_4_pin11), .pin12(_7448_4_pin12), .pin13(_7448_4_pin13), .pin14(_7448_4_pin14),
    .pin15(_7448_4_pin15), .pin16(1'b1));
  _7448 _7448_5 (
    .pin1(_7448_5_pin1), .pin2(_7448_5_pin2), .pin3(1'b1), .pin4(1'b1), .pin5(1'b1), .pin6(_7448_5_pin6),
    .pin7(_7448_5_pin7), .pin8(1'b0), .pin9(_7448_5_pin9), .pin10(_7448_5_pin10), .pin11(_7448_5_pin11),
    .pin12(_7448_5_pin12), .pin13(_7448_5_pin13), .pin14(_7448_5_pin14), .pin15(_7448_5_pin15), .pin16(1'b1));
  // Embedded_Mod_60_Counter embedded_mod_60_counter_2: pin names not known; wires that end beside it: _7448_4_pin1, embedded_mod_60_counter_2_p2, _7448_4_pin2, embedded_mod_24_counter_1_p1, embedded_mod_60_counter_2_p5, _7448_5_pin7, _7448_5_pin1, _7448_5_pin2, _7448_5_pin6, embedded_mod_60_counter_2_p10
  Seven_Seg seven_seg_5 (
    .a(_7448_6_pin13), .b(_7448_6_pin12), .c(_7448_6_pin11), .d(_7448_6_pin10), .e(_7448_6_pin9),
    .f(_7448_6_pin15), .g(_7448_6_pin14), .dp(1'b0));
  Seven_Seg seven_seg_6 (
    .a(_7448_5_pin13), .b(_7448_5_pin12), .c(_7448_5_pin11), .d(_7448_5_pin10), .e(_7448_5_pin9),
    .f(_7448_5_pin15), .g(_7448_5_pin14), .dp(1'b1));
  _7448 _7448_6 (
    .pin1(_7448_6_pin1), .pin2(_7448_6_pin2), .pin3(1'b1), .pin4(1'b1), .pin5(1'b1), .pin6(1'b0),
    .pin7(embedded_mod_60_counter_2_p10), .pin8(1'b0), .pin9(_7448_6_pin9), .pin10(_7448_6_pin10),
    .pin11(_7448_6_pin11), .pin12(_7448_6_pin12), .pin13(_7448_6_pin13), .pin14(_7448_6_pin14),
    .pin15(_7448_6_pin15), .pin16(1'b1));
  _7448 _7448_7 (
    .pin1(_7448_7_pin1), .pin2(_7448_7_pin2), .pin3(1'b1), .pin4(1'b1), .pin5(1'b1), .pin6(_7448_7_pin6),
    .pin7(_7448_7_pin7), .pin8(1'b0), .pin9(_7448_7_pin9), .pin10(_7448_7_pin10), .pin11(_7448_7_pin11),
    .pin12(_7448_7_pin12), .pin13(_7448_7_pin13), .pin14(_7448_7_pin14), .pin15(_7448_7_pin15), .pin16(1'b1));
  // Embedded_Mod_100_Counter embedded_mod_100_counter_1: pin names not known; wires that end beside it: _7448_6_pin1, embedded_mod_60_counter_2_p2, _7448_6_pin2, embedded_mod_60_counter_1_p4, embedded_mod_100_counter_1_p5, _7448_7_pin7, _7448_7_pin1, _7448_7_pin2, _7448_7_pin6, embedded_mod_100_counter_1_p10, embedded_mod_100_counter_1_p11, embedded_mod_100_counter_1_p12
  Seven_Seg seven_seg_7 (
    .a(_7448_8_pin13), .b(_7448_8_pin12), .c(_7448_8_pin11), .d(_7448_8_pin10), .e(_7448_8_pin9),
    .f(_7448_8_pin15), .g(_7448_8_pin14), .dp(1'b0));
  Seven_Seg seven_seg_8 (
    .a(_7448_7_pin13), .b(_7448_7_pin12), .c(_7448_7_pin11), .d(_7448_7_pin10), .e(_7448_7_pin9),
    .f(_7448_7_pin15), .g(_7448_7_pin14), .dp(1'b0));
  _7448 _7448_8 (
    .pin1(embedded_mod_100_counter_1_p11), .pin2(embedded_mod_100_counter_1_p12), .pin3(1'b1), .pin4(1'b1),
    .pin5(1'b1), .pin6(_7448_8_pin6), .pin7(embedded_mod_100_counter_1_p10), .pin8(1'b0),
    .pin9(_7448_8_pin9), .pin10(_7448_8_pin10), .pin11(_7448_8_pin11), .pin12(_7448_8_pin12),
    .pin13(_7448_8_pin13), .pin14(_7448_8_pin14), .pin15(_7448_8_pin15), .pin16(1'b1));
  or or_1 (embedded_mod_60_counter_2_p2, embedded_mod_60_counter_1_p2, CLR);
  and and_1 (embedded_mod_100_counter_1_p5, START, CLK);

  // Notes on the sheet:
  //   CLK: Hz: 100
endmodule
